// Digital circuit address_decoder.dig as structural Verilog
module address_decoder (
  input  A8,
  input  A9,
  input  A10,
  input  A11,
  input  A12,
  input  A13,
  input  A14,
  input  A15,
  input  VMA,
  input  R_W,
  input  Clock,
  output WriteOut,
  output ClockOut
);

  wire nor_1_out, nor_2_out, not_1_out, or_1_out;

  not not_1 (not_1_out, R_W);
  nor nor_1 (nor_1_out, A8, A9, A10, A11, A12, A13, A14, A15);
  nor nor_2 (nor_2_out, A10, A11, ~A12, A13, A14, A15);  // NOr
  or or_1 (or_1_out, nor_1_out, nor_2_out);
  and and_1 (WriteOut, or_1_out, VMA, not_1_out);

  assign ClockOut = Clock;

  // Notes on the sheet:
  //   A8: pin 1
  //   A9: pin 2
  //   A10: pin 3
  //   A11: pin 4
  //   A12: pin 5
  //   A13: pin 6
  //   A14: pin 7
  //   A15: pin 8
  //   VMA: Valid Memory Address, pin 19
  //   R_W: Read (high) / Write (low), pin 18
  //   Clock: pin 9
  //   WriteOut: pin 13
  //   ClockOut: pin 12
endmodule
