// Digital circuit sys7-address-decode.dig as structural Verilog
module sys7_address_decode (
  input  A13,
  input  A14,
  input  A9,
  input  A12,
  input  A8,
  output RAM_Write_Enable,
  output CMOS_Ram
);

  wire and_1_out, nand_1_out, nand_2_out, nand_3_out, nor_1_out, nor_2_out, not_3_out;

  not not_1 (CMOS_Ram, nand_1_out);
  nand nand_1 (nand_1_out, not_3_out, 1'b1, nor_2_out);
  not not_2 (RAM_Write_Enable, nand_2_out);
  nor nor_1 (nor_1_out, A9, A12);
  not not_3 (not_3_out, nand_3_out);
  nand nand_2 (nand_2_out, nand_3_out, and_1_out);
  nand nand_3 (nand_3_out, A8, nor_1_out);
  and and_1 (and_1_out, 1'b1, nor_2_out);
  nor nor_2 (nor_2_out, A14, A13);

  // Notes on the sheet:
  //   A9: Schematic says A7, but in reality it's A9
endmodule
